# Fritzing sketch Luxmeter (saved by Fritzing 0.9.3b)

parts:
  Part1 = Arduino Nano (Rev3.0)
  OLED_I2C1 = OLED 128x64 I2C Monochrome Display
  e-radionica_com2 = LM393 LDR breakout [part_number=100027]

nets:
  GND: Part1.GND, OLED_I2C1.GND, e-radionica_com2.GND
  5V: Part1.5V, e-radionica_com2.VCC
  N1: Part1.A5, OLED_I2C1.SCK
  N2: Part1.A4, OLED_I2C1.SDA
  N3: Part1.A0, e-radionica_com2.AO
